# Fritzing sketch Garden Sensors (saved by Fritzing 1.0.4)

parts:
  Part1 = Solar Cell
  TP1 = TP4056 [chip_label=TP4056 package="DIP (Dual Inline) [THT]"]
  DHT1 = dht22
  Capacitive_Soil_Moisture_Sensor1 = Capacitive Soil Moisture Sensor V2.0
  YL-83_-_Detection_Board1 = YL-83 Rain Sensor - Detection Board
  YL-83_-_Control_Board1 = YL-83 Rain Sensor - Control Board
  DS1 = DS18B20 1-Wire Temperature Sensor Probe Cable
  SW1 = DIP Switch 4 Position [package=dipswitch-04]
  Part2 = VEML7700 [part_number="Adafruit #4162"]
  Mod1 = Raspberry Pi Pico W
  VCC1 = Battery

nets:
  N1: Part1.+, TP1.pin1
  N2: Part1.-, TP1.pin2
  N3: TP1.pin3, Mod1.pin_39
  N4: TP1.pin4, VCC1.+
  N5: TP1.pin5, VCC1.-
  N6: TP1.pin6, Mod1.pin_40
  N7: DHT1.connector0, Mod1.pin_21
  N8: DHT1.connector1, Mod1.pin_22
  GND: DHT1.connector3, Capacitive_Soil_Moisture_Sensor1.GND, YL-83_-_Control_Board1.GND, DS1.GND, SW1.4, Part2.GND, Mod1.pin_3, Mod1.pin_13, Mod1.pin_18, Mod1.pin_23, Mod1.pin_28, Mod1.pin_33, Mod1.pin_42
  N9: Capacitive_Soil_Moisture_Sensor1.AOUT, Mod1.pin_31
  N10: Capacitive_Soil_Moisture_Sensor1.VCC, Mod1.pin_29
  N11: YL-83_-_Detection_Board1.POS, YL-83_-_Control_Board1.POS
  N12: YL-83_-_Detection_Board1.NEG, YL-83_-_Control_Board1.NEG
  N13: YL-83_-_Control_Board1.VCC, Mod1.pin_27
  N14: YL-83_-_Control_Board1.DO, Mod1.pin_26
  N15: DS1.DQ, Mod1.pin_20
  N16: DS1.VDD, Mod1.pin_19
  N17: SW1.5, Mod1.pin_12
  N18: SW1.6, Mod1.pin_11
  N19: SW1.7, Mod1.pin_10
  N20: SW1.8, Mod1.pin_9
  N21: Part2.VIN, Mod1.pin_4
  N22: Part2.SCL, Mod1.pin_2
  N23: Part2.SDA, Mod1.pin_1

notes:
  Parallel

custom parts:
  TP4056: A DIP stand-in part for whatever IC you want. With 6 pins on a 300mil dual inline package (DIP) footprint.
  YL-83 Rain Sensor - Detection Board: The YL-83 is a rain sensor that has more resistance when dry and less resistance when wet. The module runs at 5V.
  YL-83 Rain Sensor - Control Board: The YL-83 is a rain sensor that has more resistance when dry and less resistance when wet. The module runs at 5V.
  Raspberry Pi Pico W: Raspberry Pi Pico W. Based around the RP2040 microcontroller the Pico W is a low cost microcontroller device bringing Raspberry Pi quality, cost, and easy of use to the microcontroller space. The areas marked KEEPOUT in pcb silkscreen should not have traces running through them to avoid shorts on a soldered in module!
  Battery: Your standard 2x 18650 battery pack (14.7 Volts)
