# Fritzing sketch Watertank Sensors (saved by Fritzing 1.0.4)
breadboards: 1

parts:
  Part3 = Solar Cell
  TP2 = TP4056 [chip_label=TP4056 package="DIP (Dual Inline) [THT]"]
  SW2 = DIP Switch 4 Position [package=dipswitch-04]
  Mod2 = Raspberry Pi Pico W
  VCC2 = Battery
  M1 = water level switch
  M2 = water level switch
  M3 = water level switch
  M4 = water level switch
  M5 = water level switch
  M6 = water level switch
  M7 = water level switch
  M8 = water level switch

nets:
  N1: Part3.+, TP2.pin1
  N2: Part3.-, TP2.pin2
  N3: TP2.pin3, Mod2.pin_39
  N4: TP2.pin4, VCC2.+
  N5: TP2.pin5, VCC2.-
  N6: TP2.pin6, Mod2.pin_40
  N7: SW2.4, Mod2.pin_3, Mod2.pin_13, Mod2.pin_28, Mod2.pin_33, Mod2.pin_42, M1.pin1, M2.pin1, M3.pin1, M4.pin1, M5.pin1, M6.pin1, M7.pin1, M8.pin1
  N8: SW2.5, Mod2.pin_12
  N9: SW2.6, Mod2.pin_11
  N10: SW2.7, Mod2.pin_10
  N11: SW2.8, Mod2.pin_9
  N12: Mod2.pin_1, M1.pin2
  N13: Mod2.pin_2, M4.pin2
  N14: Mod2.pin_4, M3.pin2
  N15: Mod2.pin_5, M2.pin2
  N16: Mod2.pin_24, M5.pin2
  N17: Mod2.pin_25, M7.pin2
  N18: Mod2.pin_26, M6.pin2
  N19: Mod2.pin_27, M8.pin2

notes:
  Parallel
  These are not the same sensors but simular

custom parts:
  TP4056: A DIP stand-in part for whatever IC you want. With 6 pins on a 300mil dual inline package (DIP) footprint.
  Raspberry Pi Pico W: Raspberry Pi Pico W. Based around the RP2040 microcontroller the Pico W is a low cost microcontroller device bringing Raspberry Pi quality, cost, and easy of use to the microcontroller space. The areas marked KEEPOUT in pcb silkscreen should not have traces running through them to avoid shorts on a soldered in module!
  Battery: Your standard 2x 18650 battery pack (14.7 Volts)
  water level switch: Generic water level float switch.
